// Logisim project TP.circ as structural Verilog: 3 circuits, main circuit main
module main (
  input  in_1,
  input  in_2
);

  wire banc_reg_1_p2, banc_reg_1_p8, decodeur_1_imm_reg;
  wire [1:0] decodeur_1_op;
  wire [3:0] decodeur_1_rd, decodeur_1_rot, decodeur_1_rs1, decodeur_1_rs2;
  wire [7:0] decodeur_1_imm;
  wire [31:0] adder_1_out, banc_reg_1_p9, calculateur_immediat_1_out_3, multiplexer_1_out, PC_q, ram_1_dout;

  Register #(.width(32)) PC (.D(adder_1_out), .en(1'b1), .clk(in_1), .Q(PC_q));  // open: clr
  RAM #(.addrWidth(24), .asyncread("true"), .dataWidth(32)) ram_1 (
    .addr(PC_q[25:2]), .oe(1'b1), .dout(ram_1_dout));  // open: we, clk, din
  Adder #(.width(32)) adder_1 (.a(PC_q), .b(32'h4), .out(adder_1_out));  // open: cin, cout
  // Probe on ram_1_dout
  // Probe on {{8{1'b0}}, PC_q[23:0]}
  decodeur decodeur_1 (
    .in_1(ram_1_dout), .Rd(decodeur_1_rd), .Rs1(decodeur_1_rs1), .Rs2(decodeur_1_rs2), .Op(decodeur_1_op),
    .Imm_reg(decodeur_1_imm_reg), .Imm(decodeur_1_imm), .Rot(decodeur_1_rot));
  calculateur_immediat calculateur_immediat_1 (
    .Imm(decodeur_1_imm), .Rot(decodeur_1_rot), .out_3(calculateur_immediat_1_out_3));
  // Probe on decodeur_1_rs1
  // Probe on decodeur_1_rs2
  // Probe on decodeur_1_rd
  // Probe on calculateur_immediat_1_out_3
  // banc_reg banc_reg_1: pin names not known; wires that end beside it: in_1, banc_reg_1_p2, decodeur_1_rs1, decodeur_1_rs2, decodeur_1_rd, in_2, {{8{1'b0}}, PC_q[23:0]}, banc_reg_1_p8, banc_reg_1_p9
  // Probe on banc_reg_1_p9
  Multiplexer #(.width(32)) multiplexer_1 (
    .in0(banc_reg_1_p9), .in1(calculateur_immediat_1_out_3), .out(multiplexer_1_out), .sel(decodeur_1_imm_reg));
  // Probe on multiplexer_1_out
  // ALU alu_1: pin names not known; wires that end beside it: banc_reg_1_p8, multiplexer_1_out, decodeur_1_op, banc_reg_1_p2
  // Probe on banc_reg_1_p2
endmodule

module decodeur (
  input  [31:0] in_1,
  output [3:0] Rd,
  output [3:0] Rs1,
  output [3:0] Rs2,
  output [1:0] Op,
  output Imm_reg,
  output [7:0] Imm,
  output [3:0] Rot
);

  wire and_1_out, not_1_out;

  not not_1 (not_1_out, in_1[24]);
  and and_1 (and_1_out, in_1[23], not_1_out);
  or or_1 (Op[0], in_1[21], in_1[22]);
  or or_2 (Op[1], in_1[22], and_1_out);

  assign Imm = in_1[7:0];
  assign Imm_reg = in_1[25];
  assign Rd = in_1[15:12];
  assign Rot = in_1[11:8];
  assign Rs1 = in_1[19:16];
  assign Rs2 = in_1[3:0];
endmodule

module calculateur_immediat (
  input  [7:0] Imm,
  input  [3:0] Rot,
  output [31:0] out_3
);

  Shifter #(.shift("rr"), .width(32)) shifter_1 (.in({{25{Imm[7]}}, Imm[6:0]}), .\dist ({Rot, 1'b0}), .out(out_3));
endmodule
